# Fritzing sketch recordAndPlayback (saved by Fritzing 0.8.5b)
breadboards: 1

parts:
  Part1 = Arduino Uno (Rev3)
  S1 = Pushbutton [package="[THT]"]
  S2 = Pushbutton [package="[THT]"]
  LED1 = LED - 5mm [color="Red (633nm)" package="5 mm [THT]"]
  R1 = Resistor [tolerance=±5% resistance=10k package=THT]
  R2 = Resistor [tolerance=±5% resistance=10k package=THT]
  R3 = Resistor [tolerance=±5% resistance=220 package=THT]
  S3 = Pushbutton [package="[THT]"]
  S4 = Pushbutton [package="[THT]"]
  R4 = Resistor [tolerance=±5% resistance=10k package=THT]
  R5 = Resistor [tolerance=±5% resistance=10k package=THT]

nets:
  N1: Part1.D8, S3.Pin_1, S3.Pin_2, R4.Pin_0
  N2: Part1.D9_PWM, LED1.anode
  N3: Part1.D10_PWM/SS, S4.Pin_1, S4.Pin_2, R5.Pin_0
  N4: Part1.GND, R1.Pin_1, R2.Pin_1, R3.Pin_1, R4.Pin_1, R5.Pin_1
  N5: Part1.D4, S1.Pin_1, S1.Pin_2, R1.Pin_0
  N6: Part1.D6_PWM, S2.Pin_1, S2.Pin_2, R2.Pin_0
  N7: Part1.5V, S1.Pin_3, S1.Pin_4, S2.Pin_3, S2.Pin_4, S3.Pin_3, S3.Pin_4, S4.Pin_3, S4.Pin_4
  N8: LED1.cathode, R3.Pin_0

notes:
  speed controls
  mode and morse controls
